# Fritzing sketch Temp Display Sketch (saved by Fritzing 0.9.3b)
circuit board: 8.46667cm x 5.64444cm
breadboards: 1

parts:
  Part1 = Arduino Nano 33 IOT
  S1 = Pushbutton [package="[SMD]"]
  AM1 = AM2320 Humidity and Temperature Sensor [part_number="Adafruit #3721"]
  R1 = Resistor [tolerance=±5% resistance=10k package=THT]
  R2 = Resistor [tolerance=±5% resistance=10k package=THT]
  Part2 = OLED Monochrome 128x32 I2C [part_number=931]

nets:
  N1: Part1.RESET, Part1.A7
  GND: Part1.GND, Part1.D13~, S1.Pin_1, S1.Pin_2, AM1.GND, Part2.GND
  N2: Part1.D2, S1.Pin_3, S1.Pin_4
  N3: Part1.D11/MOSI, Part1.+5V
  N4: Part1.A5, AM1.SCL, R1.Pin_0, Part2.SCL
  N5: Part1.A4, AM1.SDA, R2.Pin_1, Part2.SDA
  3V3: Part1.3V3, AM1.VDD, R1.Pin_1, R2.Pin_0, Part2.3.3V

custom parts:
  Arduino Nano 33 IOT: The Arduino Nano 33 IoT is the easiest and cheapest point of entry to enhance existing devices (and creating new ones) to be part of the IoT and designing pico-network applications. Whether you are looking at building a sensor network connected to your office or home router, or if you want to create a BLE device sending data to a cellphone, the Nano 33 IoT is your one-stop-solution for many of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
  AM2320 Humidity and Temperature Sensor: AM2320 I2C Humidity and Temperature Sensor
  OLED Monochrome 128x32 I2C: These displays are small, only about 1" diagonal, but very readable due to the high contrast of an OLED display. This display is made of 128x32 individual white OLED pixels, each one is turned on or off by the controller chip. Because the display makes its own light, no backlight is required. This reduces the power required to run the OLED and is why the display has such high contrast; we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
